// Logisim project lab6.circ as structural Verilog: 1 circuit, main circuit main
module main (
  input  [3:0] in_1,
  input  [3:0] in_2,
  input  C0,
  output out_4,
  output C1,
  output [4:0] out_6,
  output out_7,
  output C2,
  output out_9,
  output C3,
  output out_11,
  output C4
);

  wire and_1_out, and_2_out, and_3_out, and_4_out, and_5_out, and_6_out, and_7_out, and_8_out, and_9_out,
       and_10_out, G0_out, G1_out, G2_out, G3_out, P0_out, P1_out, P2_out, P3_out;

  xor P0 (P0_out, in_1[0], in_2[0]);
  and and_1 (and_1_out, in_1[0], C0);
  and G0 (G0_out, in_1[0], in_2[0]);
  xor P1 (P1_out, in_2[1], in_1[1]);
  and G1 (G1_out, in_2[1], in_1[1]);
  xor P2 (P2_out, in_2[2], in_1[2]);
  and G2 (G2_out, in_2[2], in_1[2]);
  xor P3 (P3_out, in_2[3], in_1[3]);
  and G3 (G3_out, in_2[3], in_1[3]);
  xor xor_1 (out_4, P0_out, C0);
  or or_1 (C1, and_1_out, G0_out);
  xor xor_2 (out_6[1], P1_out, C1);
  and and_2 (and_2_out, P1_out, G0_out);
  and and_3 (and_3_out, P1_out, P0_out, C0);
  xor xor_3 (out_6[2], P2_out, C2);
  and and_4 (and_4_out, P2_out, G1_out);
  and and_5 (and_5_out, P2_out, P1_out, G0_out);
  and and_6 (and_6_out, P2_out, P1_out, P0_out, C0);
  xor xor_4 (out_6[3], P3_out, C3);
  and and_7 (and_7_out, P3_out, G2_out);
  and and_8 (and_8_out, P3_out, P2_out, G1_out);
  and and_9 (and_9_out, P3_out, P2_out, P1_out, C0);
  and and_10 (and_10_out, P3_out, P2_out, P1_out, P0_out, C0);
  ExactlyOne xor_5 (.out(C2), .in0(G1_out), .in1(and_2_out), .in2(and_3_out));
  or or_2 (C3, G2_out, and_4_out, and_5_out, and_6_out);
  ExactlyOne xor_6 (.out(C4), .in0(G3_out), .in1(and_7_out), .in2(and_8_out), .in3(and_9_out), .in4(and_10_out));

  assign {out_6[4], out_6[0]} = {C4, out_4};
  assign out_7 = out_6[1];
  assign out_9 = out_6[2];
  assign out_11 = out_6[3];
endmodule
