// Logisim project lab6_2.circ as structural Verilog: 1 circuit, main circuit main
module main (
  input  [3:0] in_1,
  input  [3:0] in_2
);

  wire nor_1_out, nor_2_out, nor_3_out, nor_4_out, nor_5_out, nor_6_out, nor_7_out, nor_8_out, nor_9_out,
       nor_10_out, nor_11_out, nor_12_out, nor_13_out, nor_14_out, nor_15_out, nor_16_out, nor_17_out,
       nor_18_out, nor_19_out, nor_20_out, nor_21_out, nor_22_out, nor_23_out, nor_24_out, nor_25_out,
       nor_26_out, nor_27_out, nor_28_out, nor_29_out, nor_30_out, nor_31_out, nor_32_out, nor_33_out,
       nor_34_out, nor_35_out, nor_36_out, nor_37_out, nor_38_out, nor_39_out, nor_40_out, nor_41_out,
       nor_42_out, nor_43_out, nor_44_out, nor_45_out, nor_46_out, nor_47_out, nor_48_out, nor_49_out,
       nor_50_out, nor_51_out, nor_52_out, nor_53_out, nor_54_out, nor_55_out, nor_56_out, nor_57_out,
       nor_58_out, nor_59_out, nor_60_out, nor_61_out, nor_62_out, nor_63_out, nor_64_out, nor_65_out,
       nor_66_out, nor_67_out, nor_68_out, nor_69_out, nor_70_out, nor_71_out, nor_72_out, nor_73_out,
       nor_74_out, nor_75_out, nor_76_out, nor_77_out, nor_78_out, nor_79_out, nor_80_out, nor_81_out,
       nor_82_out, nor_83_out, nor_84_out, nor_85_out, nor_86_out, nor_87_out, nor_88_out, nor_89_out,
       nor_90_out, nor_91_out, nor_92_out, nor_93_out;

  nor nor_1 (nor_1_out, in_1[3], in_1[3]);
  nor nor_2 (nor_2_out, in_2[3], in_2[3]);
  nor nor_3 (nor_3_out, in_1[2], in_1[2]);
  nor nor_4 (nor_4_out, in_2[2], in_2[2]);
  nor nor_5 (nor_5_out, in_1[1], in_1[1]);
  nor nor_6 (nor_6_out, in_2[1], in_2[1]);
  nor nor_7 (nor_7_out, in_1[0], in_1[0]);
  nor nor_8 (nor_8_out, in_2[0], in_2[0]);
  nor nor_9 (nor_9_out, in_1[3], in_1[3]);
  nor nor_10 (nor_10_out, nor_2_out, nor_2_out);
  nor nor_11 (nor_11_out, in_2[3], in_2[3]);
  nor nor_12 (nor_12_out, nor_1_out, nor_1_out);
  nor nor_13 (nor_13_out, in_1[2], in_1[2]);
  nor nor_14 (nor_14_out, nor_4_out, nor_4_out);
  nor nor_15 (nor_15_out, in_2[2], in_2[2]);
  nor nor_16 (nor_16_out, nor_3_out, nor_3_out);
  nor nor_17 (nor_17_out, in_1[1], in_1[1]);
  nor nor_18 (nor_18_out, nor_6_out, nor_6_out);
  nor nor_19 (nor_19_out, in_2[1], in_2[1]);
  nor nor_20 (nor_20_out, nor_5_out, nor_5_out);
  nor nor_21 (nor_21_out, in_1[0], in_1[0]);
  nor nor_22 (nor_22_out, nor_8_out, nor_8_out);
  nor nor_23 (nor_23_out, in_2[0], in_2[0]);
  nor nor_24 (nor_24_out, nor_7_out, nor_7_out);
  nor nor_25 (nor_25_out, nor_9_out, nor_10_out);
  nor nor_26 (nor_26_out, nor_11_out, nor_12_out);
  nor nor_27 (nor_27_out, nor_13_out, nor_14_out);
  nor nor_28 (nor_28_out, nor_15_out, nor_16_out);
  nor nor_29 (nor_29_out, nor_17_out, nor_18_out);
  nor nor_30 (nor_30_out, nor_19_out, nor_20_out);
  nor nor_31 (nor_31_out, nor_21_out, nor_22_out);
  nor nor_32 (nor_32_out, nor_23_out, nor_24_out);
  nor nor_33 (nor_33_out, nor_25_out, nor_26_out);
  nor nor_34 (nor_34_out, nor_27_out, nor_28_out);
  nor nor_35 (nor_35_out, nor_29_out, nor_30_out);
  nor nor_36 (nor_36_out, nor_31_out, nor_32_out);
  nor nor_37 (nor_37_out, nor_33_out, nor_33_out);
  nor nor_38 (nor_38_out, nor_27_out, nor_27_out);
  nor nor_39 (nor_39_out, nor_33_out, nor_33_out);
  nor nor_40 (nor_40_out, nor_28_out, nor_28_out);
  nor nor_41 (nor_41_out, nor_31_out, nor_31_out);
  nor nor_42 (nor_42_out, nor_34_out, nor_34_out);
  nor nor_43 (nor_43_out, nor_33_out, nor_33_out);
  nor nor_44 (nor_44_out, nor_35_out, nor_35_out);
  nor nor_45 (nor_45_out, nor_33_out, nor_33_out);
  nor nor_46 (nor_46_out, nor_34_out, nor_34_out);
  nor nor_47 (nor_47_out, nor_35_out, nor_35_out);
  nor nor_48 (nor_48_out, nor_32_out, nor_32_out);
  nor nor_49 (nor_49_out, nor_37_out, nor_38_out);
  nor nor_50 (nor_50_out, nor_39_out, nor_40_out);
  nor nor_51 (nor_51_out, nor_41_out, nor_42_out);
  nor nor_52 (nor_52_out, nor_43_out, nor_44_out);
  nor nor_53 (nor_53_out, nor_45_out, nor_46_out);
  nor nor_54 (nor_54_out, nor_47_out, nor_48_out);
  nor nor_55 (nor_55_out, nor_33_out, nor_33_out);
  nor nor_56 (nor_56_out, nor_34_out, nor_34_out);
  nor nor_57 (nor_57_out, nor_35_out, nor_35_out);
  nor nor_58 (nor_58_out, nor_36_out, nor_36_out);
  nor nor_59 (nor_59_out, nor_55_out, nor_56_out);
  nor nor_60 (nor_60_out, nor_57_out, nor_58_out);
  nor nor_61 (nor_61_out, nor_29_out, nor_29_out);
  nor nor_62 (nor_62_out, nor_34_out, nor_34_out);
  nor nor_63 (nor_63_out, nor_33_out, nor_33_out);
  nor nor_64 (nor_64_out, nor_34_out, nor_34_out);
  nor nor_65 (nor_65_out, nor_50_out, nor_90_out);
  nor nor_66 (nor_66_out, nor_26_out, nor_78_out);
  nor nor_67 (nor_67_out, nor_51_out, nor_51_out);
  nor nor_68 (nor_68_out, nor_52_out, nor_52_out);
  nor nor_69 (nor_69_out, nor_53_out, nor_53_out);
  nor nor_70 (nor_70_out, nor_54_out, nor_54_out);
  nor nor_71 (nor_71_out, nor_25_out, nor_49_out);
  nor nor_72 (nor_72_out, nor_89_out, nor_77_out);
  nor nor_73 (nor_73_out, nor_59_out, nor_59_out);
  nor nor_74 (nor_74_out, nor_60_out, nor_60_out);
  nor nor_75 (nor_75_out, nor_61_out, nor_62_out);
  nor nor_76 (nor_76_out, nor_63_out, nor_64_out);
  nor nor_77 (nor_77_out, nor_67_out, nor_68_out);
  nor nor_78 (nor_78_out, nor_69_out, nor_70_out);
  nor nor_79 (nor_79_out, nor_73_out, nor_74_out);
  nor nor_80 (nor_80_out, nor_65_out, nor_65_out);
  nor nor_81 (nor_81_out, nor_66_out, nor_66_out);
  nor nor_82 (nor_82_out, nor_71_out, nor_71_out);
  nor nor_83 (nor_83_out, nor_72_out, nor_72_out);
  LED led_1 (.in(nor_79_out));
  nor nor_84 (nor_84_out, nor_75_out, nor_75_out);
  nor nor_85 (nor_85_out, nor_33_out, nor_33_out);
  nor nor_86 (nor_86_out, nor_76_out, nor_76_out);
  nor nor_87 (nor_87_out, nor_30_out, nor_30_out);
  nor nor_88 (nor_88_out, nor_82_out, nor_83_out);
  nor nor_89 (nor_89_out, nor_84_out, nor_85_out);
  nor nor_90 (nor_90_out, nor_86_out, nor_87_out);
  nor nor_91 (nor_91_out, nor_80_out, nor_81_out);
  nor nor_92 (nor_92_out, nor_88_out, nor_88_out);
  nor nor_93 (nor_93_out, nor_91_out, nor_91_out);
  LED led_2 (.in(nor_92_out));
  LED led_3 (.in(nor_93_out));

  // Notes on the sheet:
  //   X3'
  //   X2'
  //   X1'
  //   X0'
  //   A=B
  //   A>B
  //   A<B
endmodule
